# Fritzing sketch Bigshot (saved by Fritzing 0.9.3b)
circuit board: 3.96461cm x 4.59428cm
breadboards: 1

parts:
  Pololu = Pololu A4988 [package=SO16]
  JP4 = Header 4 [package=molex-1x4_lock]
  JP5 = Header 3 [package=molex-1x3_lock]
  part = Arduino Pro Mini (5V)
  JP3 = Header 2 [package=molex-1x2_lock]
  U1 = POT [package=3362u]
  C1 = Capacitor Polarized [package=cpol-radial-10uf-25v]

nets:
  N1: Pololu.RESET, Pololu.SLEEP
  N2: Pololu.STEP, part.D9
  N3: Pololu.DIR, part.D8
  GND: Pololu.GND, JP5.2, part.GND, JP3.1, U1.E, C1.-
  VDD: Pololu.VDD, part.VCC
  N4: Pololu.1B, JP4.4
  N5: Pololu.1A, JP4.3
  N6: Pololu.2A, JP4.2
  N7: Pololu.2B, JP4.1
  N8: Pololu.VMOT, part.RAW, JP3.2, U1.A, C1.+
  N9: JP5.1, part.D2
  N10: JP5.3, part.D3
  N11: part.A0, U1.S
